// Logisim project alu.circ as structural Verilog: 1 circuit, main circuit alu
module alu (
  input  [31:0] A,
  input  [31:0] B,
  input  [3:0] ALUSel,
  output [31:0] Result
);

  wire [0:0] slt7;
  wire [31:0] add0, and1, divu8, mulh14, mulhu11, mulu10, or2, remu9, sll6, sra5, srl4, sub12, xor3;
  wire [31:31] multiplier_1_cout;

  Multiplier #(.width(32)) multiplier_1 (.a(A), .b(B), .cout({multiplier_1_cout[31], mulh14[30:0]}));  // open: out, cin
  Comparator #(.width(32)) comparator_1 (.a(A), .b(B), .lt(slt7[0]));  // open: gt, eq
  xor xor_1 (mulh14[31], A[31], B[31]);
  Adder #(.width(32)) adder_1 (.a(A), .b(B), .out(add0));  // open: cin, cout
  assign and1 = A & B;  // AND_Gate and_1, 32 bits wide
  assign or2 = A | B;  // OR_Gate or_1, 32 bits wide
  Shifter #(.width(32), .shift("ar")) shifter_1 (.in(A), .\dist (B[4:0]), .out(sra5));
  Shifter #(.width(32)) shifter_2 (.in(A), .\dist (B[4:0]), .out(sll6));
  Divider #(.width(32)) divider_1 (.a(A), .b(B), .out(divu8));  // open: upper, rem
  Divider #(.width(32)) divider_2 (.a(A), .b(B), .rem(remu9));  // open: out, upper
  Multiplier #(.width(32)) multiplier_2 (.a(A), .b(B), .out(mulu10));  // open: cin, cout
  Multiplier #(.width(32)) multiplier_3 (.a(A), .b(B), .cout(mulhu11));  // open: out, cin
  Subtractor #(.width(32)) subtractor_1 (.a(A), .b(B), .out(sub12));  // open: bin, bout
  assign xor3 = A ^ B;  // XOR_Gate xor_2, 32 bits wide
  Shifter #(.width(32), .shift("lr")) shifter_3 (.in(A), .\dist (B[4:0]), .out(srl4));
  Multiplexer #(.select(4), .width(32), .enable("false")) multiplexer_1 (
    .in0(add0), .in1(and1), .in2(or2), .in3(xor3), .in4(srl4), .in5(sra5), .in6(sll6),
    .in7({{31{1'b0}}, slt7[0]}), .in8(divu8), .in9(remu9), .in10(mulu10), .in11(mulhu11), .in12(sub12),
    .in13(B), .in14(mulh14), .out(Result), .sel(ALUSel));  // open: in15

  // Other names for the same wires on the sheet: bsel13[31:0] = B

  // Notes on the sheet:
  //   INPUTS to your circuit
  //   DON'T CHANGE THE LOCATIONS OF THE INPUTS AND OUTPUTS!
  //   OUTPUT from your circuit
endmodule
