// Logisim project branch_comp.circ as structural Verilog: 1 circuit, main circuit branch_comp
module branch_comp (
  input  [31:0] rs1,
  input  [31:0] rs2,
  input  BrUn,
  output BrEq,
  output BrLt
);

  wire not_2_out, or_1_out, signedd, subtractor_1_bout;
  wire [31:0] subtractor_2_out;

  Subtractor #(.width(32)) subtractor_1 (.a(rs1), .b(rs2), .bout(subtractor_1_bout));  // open: out, bin
  Multiplexer #(.select(2), .enable("false")) multiplexer_1 (
    .in0(subtractor_1_bout), .in1(1'b0), .in2(1'b1), .in3(subtractor_1_bout), .out(signedd),
    .sel({rs1[31], rs2[31]}));
  Subtractor #(.width(32)) subtractor_2 (.a(rs1), .b(rs2), .out(subtractor_2_out));  // open: bin, bout
  not not_1 (BrEq, or_1_out);
  or or_1 (or_1_out, subtractor_2_out[0], subtractor_2_out[1], subtractor_2_out[2], subtractor_2_out[3], subtractor_2_out[4], subtractor_2_out[5], subtractor_2_out[6], subtractor_2_out[7], subtractor_2_out[8], subtractor_2_out[9], subtractor_2_out[10], subtractor_2_out[11], subtractor_2_out[12], subtractor_2_out[13], subtractor_2_out[14], subtractor_2_out[15], subtractor_2_out[17], subtractor_2_out[18], subtractor_2_out[19], subtractor_2_out[20], subtractor_2_out[21], subtractor_2_out[22], subtractor_2_out[23], subtractor_2_out[24], subtractor_2_out[25], subtractor_2_out[26], subtractor_2_out[27], subtractor_2_out[28], subtractor_2_out[29], subtractor_2_out[30], subtractor_2_out[31], subtractor_2_out[16]);
  Multiplexer #(.enable("false")) multiplexer_2 (.in0(subtractor_1_bout), .in1(signedd), .out(BrLt), .sel(not_2_out));
  not not_2 (not_2_out, BrUn);

  // Notes on the sheet:
  //   INPUTS to your circuit
  //   DON'T CHANGE THE LOCATIONS OF THE INPUTS AND OUTPUTS!
  //   OUTPUT from your circuit
endmodule
