// Logisim project cpu.circ as structural Verilog: 1 circuit, main circuit main
module main (
  input  [31:0] INSTRUCTION,
  input  CLOCK,
  output [31:0] PROGRAM_COUNTER,
  output [31:0] ra,
  output [31:0] sp,
  output [31:0] t0,
  output [31:0] t1,
  output [31:0] t2,
  output [31:0] s0,
  output [31:0] s1,
  output [31:0] a0,
  output [3:0] out_12
);

  wire A, B, branch_comp_1_breq, branch_comp_1_brlt, control_logic_1_brun, control_logic_1_memrw,
       control_logic_1_pcsel, control_logic_1_regwen;
  wire [1:0] control_logic_1_wbsel;
  wire [2:0] control_logic_1_immsel;
  wire [31:0] adder_1_out, ALURes, DMEM_p5, imm, INSTRUCTION_t, multiplexer_1_out, multiplexer_2_out,
       multiplexer_3_out, multiplexer_4_out, PC4, PROGRAM_COUNTER_t, rs1, rs2, WB;

  control_logic control_logic_1 (
    .BSel(B), .BrUn(control_logic_1_brun), .RegWEn(control_logic_1_regwen), .ImmSel(control_logic_1_immsel),
    .ASel(A), .PCSel(control_logic_1_pcsel), .BrLt(branch_comp_1_brlt), .BrEq(branch_comp_1_breq),
    .inst(INSTRUCTION_t), .ALUSel(out_12), .MemRW(control_logic_1_memrw), .WBSel(control_logic_1_wbsel));  // open: out_13
  Adder #(.width(32)) adder_1 (.a(PROGRAM_COUNTER), .b(32'h4), .out(adder_1_out));  // open: cin, cout
  Multiplexer #(.width(32), .enable("false")) multiplexer_1 (
    .in0(adder_1_out), .in1(ALURes), .out(multiplexer_1_out), .sel(control_logic_1_pcsel));
  Register #(.width(32)) PC (.D(multiplexer_1_out), .clk(CLOCK), .Q(PROGRAM_COUNTER));  // open: en, clr
  Multiplexer #(.width(32), .enable("false")) multiplexer_2 (
    .in0(INSTRUCTION), .in1(32'h13), .out(multiplexer_2_out), .sel(control_logic_1_pcsel));
  Register #(.width(32)) register_1 (.D(multiplexer_2_out), .clk(CLOCK), .Q(INSTRUCTION_t));  // open: en, clr
  Register #(.width(32)) register_2 (.D(PROGRAM_COUNTER), .clk(CLOCK), .Q(PROGRAM_COUNTER_t));  // open: en, clr
  imm_gen ImmGen (.ImmSel(control_logic_1_immsel), .imm(imm), .inst(INSTRUCTION_t));
  regfile_main RegFile (
    .rs2(INSTRUCTION_t[24:20]), .rd(INSTRUCTION_t[11:7]), .Read_Data_1(rs1), .Read_Data_2(rs2), .ra(ra),
    .sp(sp), .t0(t0), .t1(t1), .t2(t2), .s0(s0), .s1(s1), .a0(a0), .rs1(INSTRUCTION_t[19:15]),
    .Write_Data(WB), .RegWEn(control_logic_1_regwen), .clk(CLOCK));  // open: in_5
  branch_comp branch_comp_1 (
    .BrEq(branch_comp_1_breq), .rs2(rs2), .BrUn(control_logic_1_brun), .BrLt(branch_comp_1_brlt), .rs1(rs1));
  Adder #(.width(32)) adder_2 (.a(PROGRAM_COUNTER_t), .b(32'h4), .out(PC4));  // open: cin, cout
  Multiplexer #(.width(32), .enable("false")) multiplexer_3 (
    .in0(rs1), .in1(PROGRAM_COUNTER_t), .out(multiplexer_3_out), .sel(A));
  Multiplexer #(.width(32), .enable("false")) multiplexer_4 (.in0(rs2), .in1(imm), .out(multiplexer_4_out), .sel(B));
  alu Arithmetic_Logic_Unit (.Result(ALURes), .ALUSel(out_12), .A(multiplexer_3_out), .B(multiplexer_4_out));
  // mem_main DMEM: pin names not known; wires that end beside it: ALURes, rs2, CLOCK, control_logic_1_memrw, DMEM_p5
  Multiplexer #(.select(2), .width(32), .enable("false")) multiplexer_5 (
    .in0(DMEM_p5), .in1(ALURes), .in2(PC4), .out(WB), .sel(control_logic_1_wbsel));  // open: in3

  // Other names for the same wires on the sheet: clk = CLOCK; INSTRUCTION1[31:0] = INSTRUCTION;
  //   PROGRAM_COUNTER1[31:0] = PROGRAM_COUNTER

  // Notes on the sheet:
  //   Output
  //   IMEM (do **NOT** move this)
  //   Inputs
  //   It is OK to move the PC, RegFile, ALU, MEM, Branch Comp, Imm Gen, and Control Logic to wherever is most convenient for you when constructing your CPU, and to delete this text
  //   Inputs/Outputs for testing. Do **NOT** move these.
endmodule
